// Logisim project Chips.circ as structural Verilog: 1 circuit, main circuit main
module main (
  input  A_0,
  input  A_1,
  input  A_2,
  input  A_3,
  input  B_0,
  input  B_1,
  input  B_2,
  input  B_3,
  input  S_2,
  input  S_1,
  input  S_0,
  output out_12,
  output out_13,
  output out_14,
  output out_15,
  output Zero
);

  wire _2_1_AND_p3, _2_1_AND_p6, _2_1_AND_p10, _2_1_NOR_p9, _2_1_NOR_p12, _2_1_OR_p14, _8x1_MUX_2_p1,
       _8x1_MUX_2_p2, _8x1_MUX_2_p3, _8x1_MUX_3_p1, _8x1_MUX_3_p3, _8x1_MUX_4_p1, _8x1_MUX_p2, _8x1_MUX_p3,
       _8x1_MUX_p4, _8x1_MUX_p9;

  // _7408 _2_1_AND: pin names not known; wires that end beside it: A_0, B_0, _2_1_AND_p3, A_1, B_1, _2_1_AND_p6, 1'b1, A_2, B_2, _2_1_AND_p10, A_3, B_3
  // _74151 _8x1_MUX: pin names not known; wires that end beside it: 1'b0, _8x1_MUX_p2, _8x1_MUX_p3, _8x1_MUX_p4, _2_1_AND_p3, out_12, 1'b0, 1'b0, _8x1_MUX_p9, 1'b1, A_1, 1'b0, A_0, B_1, S_0, S_1, S_2
  // _74151 _8x1_MUX_2: pin names not known; wires that end beside it: _8x1_MUX_2_p1, _8x1_MUX_2_p2, _8x1_MUX_2_p3, _2_1_AND_p6, out_13, 1'b0, 1'b0, 1'b1, A_2, A_0, A_0, B_2, S_0, S_1, S_2
  // _7425 _4_1_NOR: pin names not known; wires that end beside it: out_12, out_13, out_14, out_15, Zero, 1'b0, 1'b1
  // _7402 _2_1_NOR: pin names not known; wires that end beside it: _8x1_MUX_p3, A_0, B_0, _8x1_MUX_2_p2, A_1, B_1, 1'b0, 1'b1, _2_1_NOR_p9, A_2, B_2, _2_1_NOR_p12, A_3, B_3
  // _74151 _8x1_MUX_3: pin names not known; wires that end beside it: _8x1_MUX_3_p1, _2_1_NOR_p9, _8x1_MUX_3_p3, _2_1_AND_p10, out_14, 1'b0, 1'b0, 1'b1, A_3, A_1, A_1, B_3, S_0, S_1, S_2
  // _7432 _2_1_OR: pin names not known; wires that end beside it: A_0, B_0, _8x1_MUX_p4, A_1, B_1, _8x1_MUX_2_p3, 1'b0, 1'b1, A_2, B_2, _8x1_MUX_3_p3, A_3, B_3, _2_1_OR_p14
  // _74151 _8x1_MUX_4: pin names not known; wires that end beside it: _8x1_MUX_4_p1, _2_1_NOR_p12, _2_1_OR_p14, _8x1_MUX_p9, out_15, 1'b0, 1'b0, 1'b1, 1'b0, A_2, A_2, B_0, S_0, S_1, S_2
  // _7486 _2_1_XOR: pin names not known; wires that end beside it: A_0, B_0, _8x1_MUX_p2, A_1, B_1, _8x1_MUX_2_p1, 1'b0, 1'b1, A_2, B_2, _8x1_MUX_3_p1, A_3, B_3, _8x1_MUX_4_p1, A_0, A_1, A_2, A_3, 1'b1, B_0, B_1, B_2, B_3

  // Notes on the sheet:
  //   Inputs:
  //   Vcc
  //   Grd
  //   Result
  //   Outputs
  //   Select Lines
endmodule
