// Logisim project Digital Project 1.circ as structural Verilog: 1 circuit, main circuit main
module main (
  input  A_0,
  input  A_1,
  input  A_2,
  input  A_3,
  input  B_0,
  input  B_1,
  input  B_2,
  input  B_3,
  input  [2:0] AluOP,
  input  Enable,
  output out_11,
  output Result,
  output out_13,
  output out_14,
  output Zero
);

  wire AND_3_out, AND_4_out, AND_5_out, AND_out, NOR_2_out, NOR_3_out, NOR_4_out, NOR_5_out, NOR_6_out,
       NOR_out, not_1_out, OR_2_out, OR_3_out, OR_4_out, OR_out, XOR_2_out, XOR_3_out, XOR_4_out, XOR_out;

  or OR (OR_out, A_0, B_0);
  and AND (AND_out, A_0, B_0);
  not not_1 (not_1_out, Enable);
  xor XOR (XOR_out, A_0, B_0);
  nor NOR (NOR_out, A_0, B_0);
  Multiplexer #(.select(3)) multiplexer_1 (
    .in0(AND_out), .in1(OR_out), .in2(NOR_out), .in3(XOR_out), .in4(A_1), .in5(not_1_out), .in6(A_0),
    .in7(B_1), .out(out_11), .sel(AluOP), .en(Enable));
  nor NOR_2 (NOR_2_out, out_11, Result);
  nor NOR_3 (NOR_3_out, out_13, out_14);
  and AND_2 (Zero, NOR_2_out, NOR_3_out);
  or OR_2 (OR_2_out, A_1, B_1);
  and AND_3 (AND_3_out, A_1, B_1);
  nor NOR_4 (NOR_4_out, A_1, B_1);
  xor XOR_2 (XOR_2_out, A_1, B_1);
  Multiplexer #(.select(3)) multiplexer_2 (
    .in0(AND_3_out), .in1(OR_2_out), .in2(NOR_4_out), .in3(XOR_2_out), .in4(A_2), .in5(A_0), .in6(A_0),
    .in7(B_2), .out(Result), .sel(AluOP), .en(Enable));
  and AND_4 (AND_4_out, A_2, B_2);
  nor NOR_5 (NOR_5_out, A_2, B_2);
  or OR_3 (OR_3_out, A_2, B_2);
  Multiplexer #(.select(3)) multiplexer_3 (
    .in0(AND_4_out), .in1(OR_3_out), .in2(NOR_5_out), .in3(XOR_3_out), .in4(A_3), .in5(A_1), .in6(A_1),
    .in7(B_3), .out(out_13), .sel(AluOP), .en(Enable));
  xor XOR_3 (XOR_3_out, A_2, B_2);
  or OR_4 (OR_4_out, A_3, B_3);
  and AND_5 (AND_5_out, A_3, B_3);
  Multiplexer #(.select(3)) multiplexer_4 (
    .in0(AND_5_out), .in1(OR_4_out), .in2(NOR_6_out), .in3(XOR_4_out), .in4(not_1_out), .in5(A_2), .in6(A_2),
    .in7(B_0), .out(out_14), .sel(AluOP), .en(Enable));
  nor NOR_6 (NOR_6_out, A_3, B_3);
  xor XOR_4 (XOR_4_out, A_3, B_3);

  // Notes on the sheet:
  //   4-Bit Inputs
  //   0 - AND
  //   1 - OR
  //   2 - NOR
  //   3 - XOR
  //   AluOP Functions
  //   4 - Logical Shift Left A
  //   5 - Logical Shift Right A
  //   7 - Rotate Left B
  //   6 - Arithmetic Shift Right A
endmodule
